# Fritzing sketch Telem_Remote (saved by Fritzing 0.9.3b)
breadboards: 1

parts:
  Part1 = Arduino Pro Mini v13
  Part2 = Barometric Pressure Sensor - BMP085 Breakout
  Part3 = NRF24L01+ Breakout Board
  BEC_Power = DC Power [voltage=5V]
  C1_1000uf = Capacitor Polarized [package=cpol-radial-1000uf-25v]
  C2_100uf = Capacitor Polarized [package=cpol-radial-100uf-25v]
  3_3V_Regulator = V_REG_LD1117VXX [package=78xxl]
  R1 = Resistor [tolerance=±5% resistance=1M package="2512 [SMD]"]
  R2 = Resistor [tolerance=±5% resistance=470k package="2512 [SMD]"]

nets (from the schematic view):
  VCC: Part1.VCC, Part2.VCC, BEC_Power.V+, C1_1000uf.+, 3_3V_Regulator.IN, R1.Pin_0
  GND: Part1.GND, Part2.GND, Part3.GND, BEC_Power.V-, C1_1000uf.-, C2_100uf.-, 3_3V_Regulator.GND, R2.Pin_1
  N1: Part1.A4, Part2.SDA
  N2: Part1.A5, Part2.SCL
  N3: Part1.A0, R1.Pin_1, R2.Pin_0
  N4: Part1.D13/SCK, Part3.SCK
  N5: Part1.D12/MISO, Part3.MISO
  N6: Part1.D11_PWM/MOSI, Part3.MOSI
  N7: Part1.D8, Part3.CS
  N8: Part1.D7, Part3.CE
  N9: Part3.VCC, C2_100uf.+, 3_3V_Regulator.OUT
